# Fritzing sketch pico_motorTA6586 (saved by Fritzing 0.9.3b)
breadboards: 1

parts:
  Mod1 = Raspberry Pi Pico
  Bateria = Battery block 9V
  Bateria_2 = battery_holder_single_18650 [part_number="3.7 volt"]  # not connected
  IC1 = IC, DIP package, 8 pins [chip_label=TA6586]
  M1 = DC Motor
  C1 = Ceramic Capacitor [capacitance=100nF package="100 mil [THT, multilayer]"]

nets:
  N1: Mod1.pin_3, Mod1.pin_8, Mod1.pin_13, Mod1.pin_18, Mod1.pin_23, Mod1.pin_28, Mod1.pin_33, Mod1.pin_38
  N2: Mod1.pin_19, IC1.pin1
  N3: Mod1.pin_20, IC1.pin2
  N4: Bateria.-, IC1.pin3
  N5: Bateria.+, IC1.pin4
  N6: IC1.pin5, M1.pin_2, C1.1
  N7: IC1.pin8, M1.pin_1, C1.0

custom parts:
  Raspberry Pi Pico: Raspberry Pi Pico. Based around the RP2040 microcontroller the Pico is a low cost microcontroller device bringing Raspberry Pi quality, cost, and easy of use to the microcontroller space. Jan 2021, Split part in to two versions: tht (this one) and SMD. This one will drill holes for a .1 in header in pcb to allow plugging in the module as well as providing pads to solder the module to the top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
  battery_holder_single_18650: single 18650 battery holder
